# Fritzing sketch nucleo-l476-keyword-spotting-hookup (saved by Fritzing 0.9.3b)
breadboards: 1

parts:
  J1 = STM32 Nucleo boards
  Part2 = Adafruit I2S Mic - SPH0645 [part_number="Adafruit #3421"]

nets:
  N1: J1.A2, Part2.WS
  N2: J1.D3_PWM, Part2.BCLK
  N3: J1.D4, Part2.DATA
  3V3: J1.3V3, Part2.VDD
  GND: J1.GND, Part2.GND

custom parts:
  Adafruit I2S Mic - SPH0645: For many microcontrollers, adding audio input is easy with one of our analog microphone breakouts. But as you get to bigger and better microcontrollers and microcomputers, you'll find that you don't always have an analog input, or maybe you want to avoid the noise that can seep in with an analog mic system. Once you get past 8-bit micros, you will often find an I2S peripheral, that can take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
